// Logisim project adder8.circ as structural Verilog: 21 circuits, main circuit oneBitt
module oneBitt (
  input  A,
  input  B,
  input  C,
  output S,
  output Cout
);

  wire and_1_out, and_2_out, xor_1_out;

  xor xor_1 (xor_1_out, A, B);
  xor xor_2 (S, xor_1_out, C);
  and and_1 (and_1_out, xor_1_out, C);
  and and_2 (and_2_out, A, B);
  or or_1 (Cout, and_1_out, and_2_out);
endmodule

module FourBit (
  input  [3:0] A4,
  input  [3:0] B4,
  input  Cin,
  output Cout,
  output [3:0] S4
);

  wire onebitt_1_cout, onebitt_2_cout, onebitt_3_cout;

  oneBitt onebitt_1 (.A(A4[0]), .B(B4[0]), .C(Cin), .S(S4[0]), .Cout(onebitt_1_cout));
  oneBitt onebitt_2 (.A(A4[1]), .B(B4[1]), .C(onebitt_1_cout), .S(S4[1]), .Cout(onebitt_2_cout));
  oneBitt onebitt_3 (.A(A4[2]), .B(B4[2]), .C(onebitt_2_cout), .S(S4[2]), .Cout(onebitt_3_cout));
  oneBitt onebitt_4 (.A(A4[3]), .B(B4[3]), .C(onebitt_3_cout), .S(S4[3]), .Cout(Cout));
endmodule

module EightBit (
  input  [7:0] A8,
  input  [7:0] B8,
  input  C,
  output Cout,
  output [7:0] S8
);

  wire fourbit_1_cout;

  FourBit fourbit_1 (.A4(A8[3:0]), .B4(B8[3:0]), .Cin(C), .Cout(fourbit_1_cout), .S4(S8[3:0]));
  FourBit fourbit_2 (.A4(A8[7:4]), .B4(B8[7:4]), .Cin(fourbit_1_cout), .Cout(Cout), .S4(S8[7:4]));
endmodule

module SixteenBit (
  input  [15:0] A16,
  input  [15:0] B16,
  input  Cin,
  output Cout,
  output [15:0] out_5
);

  wire eightbit_1_cout;

  EightBit eightbit_1 (.A8(A16[7:0]), .B8(B16[7:0]), .C(Cin), .Cout(eightbit_1_cout), .S8(out_5[7:0]));
  EightBit eightbit_2 (.A8(A16[15:8]), .B8(B16[15:8]), .C(eightbit_1_cout), .Cout(Cout), .S8(out_5[15:8]));
endmodule

module ALU32 (
  input  [31:0] A,
  input  [31:0] B,
  input  [3:0] Op,
  input  [4:0] Sa,
  output [31:0] C,
  output V
);

  wire addsubtractshift_1_v, equivalences_1_result, not_1_out;
  wire [31:0] addsubtractshift_1_result, bit_extender_1_out, directops_1_result, multiplexer_2_out;

  DirectOps directops_1 (.A(A), .B(B), .Sa(Op[2:1]), .result(directops_1_result));
  AddSubtractShift addsubtractshift_1 (
    .Op(Op[2:0]), .Cin(Op[2]), .Sa(Sa), .B(B), .A(A), .Result(addsubtractshift_1_result),
    .V(addsubtractshift_1_v));
  Equivalences equivalences_1 (.B(B), .A(A), .Op(Op[2:1]), .Result(equivalences_1_result));
  not not_1 (not_1_out, Op[3]);
  assign bit_extender_1_out = {{31{1'b0}}, equivalences_1_result};  // Bit_Extender bit_extender_1
  and and_1 (V, addsubtractshift_1_v, not_1_out);
  Multiplexer #(.width(32), .enable("false")) multiplexer_1 (
    .in0(addsubtractshift_1_result), .in1(multiplexer_2_out), .out(C), .sel(Op[3]));
  Multiplexer #(.width(32), .enable("false")) multiplexer_2 (
    .in0(directops_1_result), .in1(bit_extender_1_out), .out(multiplexer_2_out), .sel(Op[0]));
endmodule

module DirectOps (
  input  [31:0] A,
  input  [31:0] B,
  input  [1:0] Sa,
  output [31:0] result
);

  wire [31:0] and_1_out, nor_1_out, or_1_out, xor_1_out;

  assign and_1_out = B & A;  // AND_Gate and_1, 32 bits wide
  assign or_1_out = B | A;  // OR_Gate or_1, 32 bits wide
  assign xor_1_out = B ^ A;  // XOR_Gate xor_1, 32 bits wide
  assign nor_1_out = ~(B | A);  // NOR_Gate nor_1, 32 bits wide
  Multiplexer #(.select(2), .width(32), .enable("false")) multiplexer_1 (
    .in0(and_1_out), .in1(or_1_out), .in2(xor_1_out), .in3(nor_1_out), .out(result), .sel(Sa));
endmodule

module Reverse (
  input  [31:0] Insert,
  output [31:0] Result
);


  assign Result = {Insert[0], Insert[1], Insert[2], Insert[3], Insert[4], Insert[5], Insert[6], Insert[7], Insert[8], Insert[9], Insert[10], Insert[11], Insert[12], Insert[13], Insert[14], Insert[15], Insert[16], Insert[17], Insert[18], Insert[19], Insert[20], Insert[21], Insert[22], Insert[23], Insert[24], Insert[25], Insert[26], Insert[27], Insert[28], Insert[29], Insert[30], Insert[31]};
endmodule

module LeftShift32 (
  input  [31:0] B,
  input  [4:0] Sa,
  input  Cin,
  output [31:0] C
);

  wire [31:0] eightbitshift_1_result, fourbitshift_1_result, onebitshift_1_result, twobitshift_1_result;

  OneBitShift onebitshift_1 (.Cin(Cin), .insert(B), .OnOff(Sa[0]), .result(onebitshift_1_result));
  TwoBitShift twobitshift_1 (.Cin(Cin), .insert(onebitshift_1_result), .Onoff(Sa[1]), .result(twobitshift_1_result));
  FourBitShift fourbitshift_1 (.Cin(Cin), .OnOdd(Sa[2]), .insert(twobitshift_1_result), .result(fourbitshift_1_result));
  EightBitShift eightbitshift_1 (
    .Cin(Cin), .OnOff(Sa[3]), .insert(fourbitshift_1_result), .result(eightbitshift_1_result));
  SixteenBitShift sixteenbitshift_1 (.Cin(Cin), .OnOff(Sa[4]), .insert(eightbitshift_1_result), .result(C));
endmodule

module OneBitShift (
  input  Cin,
  input  [31:0] insert,
  input  OnOff,
  output [31:0] result
);

  Multiplexer #(.width(32), .enable("false")) multiplexer_1 (
    .in0(insert), .in1({insert[30:0], Cin}), .out(result), .sel(OnOff));
endmodule

module TwoBitShift (
  input  Cin,
  input  [31:0] insert,
  input  Onoff,
  output [31:0] result
);

  Multiplexer #(.width(32), .enable("false")) multiplexer_1 (
    .in0(insert), .in1({insert[29:0], {2{Cin}}}), .out(result), .sel(Onoff));
endmodule

module FourBitShift (
  input  Cin,
  input  OnOdd,
  input  [31:0] insert,
  output [31:0] result
);

  Multiplexer #(.width(32), .enable("false")) multiplexer_1 (
    .in0(insert), .in1({insert[27:0], {4{Cin}}}), .out(result), .sel(OnOdd));
endmodule

module EightBitShift (
  input  Cin,
  input  OnOff,
  input  [31:0] insert,
  output [31:0] result
);

  Multiplexer #(.width(32), .enable("false")) multiplexer_1 (
    .in0(insert), .in1({insert[23:0], {8{Cin}}}), .out(result), .sel(OnOff));
endmodule

module SixteenBitShift (
  input  Cin,
  input  OnOff,
  input  [31:0] insert,
  output [31:0] result
);

  Multiplexer #(.width(32), .enable("false")) multiplexer_1 (
    .in0(insert), .in1({insert[15:0], {16{Cin}}}), .out(result), .sel(OnOff));
endmodule

module Add32 (
  input  [31:0] A,
  input  Cin,
  input  [31:0] B,
  output [31:0] C,
  output V
);

  wire eightbit_1_cout, fourbit_1_cout, onebitt_1_cout, onebitt_2_cout, sixteenbit_1_cout, twobit_1_cout;
  wire [31:0] multiplexer_1_out, not_1_out;

  Multiplexer #(.width(32), .enable("false")) multiplexer_1 (
    .in0(B), .in1(not_1_out), .out(multiplexer_1_out), .sel(Cin));
  assign not_1_out = ~B;  // NOT_Gate not_1, 32 bits wide
  SixteenBit sixteenbit_1 (
    .A16(A[15:0]), .B16(multiplexer_1_out[15:0]), .Cin(Cin), .Cout(sixteenbit_1_cout), .out_5(C[15:0]));
  EightBit eightbit_1 (
    .A8(A[23:16]), .B8(multiplexer_1_out[23:16]), .C(sixteenbit_1_cout), .Cout(eightbit_1_cout), .S8(C[23:16]));
  FourBit fourbit_1 (
    .A4(A[27:24]), .B4(multiplexer_1_out[27:24]), .Cin(eightbit_1_cout), .Cout(fourbit_1_cout), .S4(C[27:24]));
  TwoBit twobit_1 (
    .A(A[29:28]), .B(multiplexer_1_out[29:28]), .Cin(fourbit_1_cout), .Result(C[29:28]), .Cout(twobit_1_cout));
  oneBitt onebitt_1 (.A(A[30]), .B(multiplexer_1_out[30]), .C(twobit_1_cout), .S(C[30]), .Cout(onebitt_1_cout));
  oneBitt onebitt_2 (.A(A[31]), .B(multiplexer_1_out[31]), .C(onebitt_1_cout), .S(C[31]), .Cout(onebitt_2_cout));
  xor xor_1 (V, onebitt_1_cout, onebitt_2_cout);
endmodule

module TwoBit (
  input  [1:0] A,
  input  [1:0] B,
  input  Cin,
  output [1:0] Result,
  output Cout
);

  wire onebitt_1_cout;

  oneBitt onebitt_1 (.A(A[0]), .B(B[0]), .C(Cin), .S(Result[0]), .Cout(onebitt_1_cout));
  oneBitt onebitt_2 (.A(A[1]), .B(B[1]), .C(onebitt_1_cout), .S(Result[1]), .Cout(Cout));
endmodule

module AddSubtractShift (
  input  [2:0] Op,
  input  Cin,
  input  [4:0] Sa,
  input  [31:0] B,
  input  [31:0] A,
  output [31:0] Result,
  output V
);

  wire add32_1_v;
  wire [31:0] add32_1_c, leftshift32_1_c, shiftright32_1_result, shiftrightarith_1_result;

  LeftShift32 leftshift32_1 (.B(B), .Sa(Sa), .Cin(Cin), .C(leftshift32_1_c));
  ShiftRightArith shiftrightarith_1 (.B(B), .Sa(Sa), .Result(shiftrightarith_1_result));
  ShiftRight32 shiftright32_1 (.B(B), .Sa(Sa), .Cin(Cin), .Result(shiftright32_1_result));
  Multiplexer #(.select(3), .width(32), .enable("false")) multiplexer_1 (
    .in0(leftshift32_1_c), .in1(leftshift32_1_c), .in2(add32_1_c), .in3(add32_1_c),
    .in4(shiftright32_1_result), .in5(shiftrightarith_1_result), .in6(add32_1_c), .in7(add32_1_c),
    .out(Result), .sel(Op));
  Add32 add32_1 (.A(A), .Cin(Op[2]), .B(B), .C(add32_1_c), .V(add32_1_v));
  and and_1 (V, Op[1], add32_1_v);
endmodule

module ShiftRight32 (
  input  [31:0] B,
  input  [4:0] Sa,
  input  Cin,
  output [31:0] Result
);

  wire not_1_out;
  wire [31:0] leftshift32_1_c, reverse_1_result;

  not not_1 (not_1_out, Cin);
  Reverse reverse_1 (.Insert(B), .Result(reverse_1_result));
  LeftShift32 leftshift32_1 (.B(reverse_1_result), .Sa(Sa), .Cin(not_1_out), .C(leftshift32_1_c));
  Reverse reverse_2 (.Insert(leftshift32_1_c), .Result(Result));
endmodule

module ShiftRightArith (
  input  [31:0] B,
  input  [4:0] Sa,
  output [31:0] Result
);

  wire [31:0] leftshift32_1_c, reverse_1_result;

  Reverse reverse_1 (.Insert(B), .Result(reverse_1_result));
  LeftShift32 leftshift32_1 (.B(reverse_1_result), .Sa(Sa), .Cin(B[31]), .C(leftshift32_1_c));
  Reverse reverse_2 (.Insert(leftshift32_1_c), .Result(Result));
endmodule

module Equivalences (
  input  [31:0] B,
  input  [31:0] A,
  input  [1:0] Op,
  output Result
);

  wire equals_1_out_3, equals_2_out_3, greaterless_1_out_2, greaterless_2_out_2, not_1_out, not_2_out;

  not not_1 (not_1_out, equals_1_out_3);
  Equals equals_1 (.A(A), .B(B), .out_3(equals_1_out_3));
  Equals equals_2 (.A(A), .B(B), .out_3(equals_2_out_3));
  GreaterLess greaterless_1 (.A(A), .out_2(greaterless_1_out_2));
  not not_2 (not_2_out, greaterless_2_out_2);
  GreaterLess greaterless_2 (.A(A), .out_2(greaterless_2_out_2));
  Multiplexer #(.select(2), .enable("false")) multiplexer_1 (
    .in0(not_1_out), .in1(equals_2_out_3), .in2(greaterless_1_out_2), .in3(not_2_out), .out(Result), .sel(Op));
endmodule

module Equals (
  input  [31:0] A,
  input  [31:0] B,
  output out_3
);

  wire [31:0] xnor_1_out;

  assign xnor_1_out = ~(B ^ A);  // XNOR_Gate xnor_1, 32 bits wide
  and and_1 (out_3, xnor_1_out[0], xnor_1_out[1], xnor_1_out[2], xnor_1_out[3], xnor_1_out[4], xnor_1_out[5], xnor_1_out[6], xnor_1_out[7], xnor_1_out[8], xnor_1_out[9], xnor_1_out[10], xnor_1_out[11], xnor_1_out[12], xnor_1_out[13], xnor_1_out[14], xnor_1_out[15], xnor_1_out[16], xnor_1_out[17], xnor_1_out[18], xnor_1_out[19], xnor_1_out[20], xnor_1_out[21], xnor_1_out[22], xnor_1_out[23], xnor_1_out[24], xnor_1_out[25], xnor_1_out[26], xnor_1_out[27], xnor_1_out[28], xnor_1_out[29], xnor_1_out[30], xnor_1_out[31]);
endmodule

module GreaterLess (
  input  [31:0] A,
  output out_2
);

  wire nor_1_out;

  nor nor_1 (nor_1_out, A[0], A[1], A[2], A[3], A[4], A[5], A[6], A[7], A[8], A[9], A[10], A[11], A[12], A[13], A[14], A[15], A[16], A[17], A[18], A[19], A[20], A[21], A[22], A[23], A[24], A[25], A[26], A[27], A[28], A[29], A[30], A[31]);
  or or_1 (out_2, A[31], nor_1_out);
endmodule
